# Fritzing sketch Laser_driver (saved by Fritzing 0.9.3b)
breadboards: 1

parts:
  U1 = 555 Timer [package="DIP8 [THT]"]
  R1 = Resistor [tolerance=±5% resistance=6.8k package=THT]
  R2 = Resistor [tolerance=±5% resistance=68k package=THT]
  C1 = Electrolytic Capacitor [capacitance=0.1mF package="100 mil [THT, electrolytic]"]
  C2 = Ceramic Capacitor [capacitance=100nF package="100 mil [THT, multilayer]"]
  Q1 = NPN-Transistor [package="TO92 [THT]"]
  Q2 = Basic FET P-Channel [package="TO220 [THT]"]
  U2 = Molex Picoblade Series Header [part_number=0533980271 package=Picoblade-53398-0271]

nets:
  N1: U1.Ground, C1.+, C2.0, Q2.source
  N2: U1.Trigger, U1.Threshold, R2.Pin_1, C1.-
  N3: U1.Output, Q1.C
  5V: U1.Reset, U1.Vcc_Supply_Voltage, R1.Pin_1
  N4: U1.Control_Voltage, C2.1
  N5: U1.Discharge, R1.Pin_0, R2.Pin_0
  N6: Q1.E, Q2.gate
  N7: Q2.drain, U2.2
  12V: U2.1

notes:
  Signal
  Laser
