# Fritzing sketch cnc_controll (saved by Fritzing 0.9.3b)
circuit board: 8.46667cm x 5.64444cm
breadboards: 1

parts:
  Part1 = Arduino Nano (Rev3.0)
  JP1_(X-end) = Header 3 [package=molex-1x3_lock]
  JP2_(Y-end) = Header 3 [package=molex-1x3_lock]
  JP3_(laser/servo) = Header 3 [package=molex-1x3_lock]
  JP5_(x-stepper) = Header 4 [package=molex-1x4_lock]
  JP6_(step_pwr) = Header 2 [package=molex-1x2_lock]
  JP4_(Y-stepper) = Header 4 [package=molex-1x4_lock]
  JP7_(step_pwr) = Header 2 [package=molex-1x2_lock]
  JP8_(power_in) = Header 3 [package=screwterminal-3.5mm-3_lock.007s]
  LED1 = LED - 5mm [color="Red (633nm)" package="5 mm [THT]"]
  LED2 = LED - 5mm [color="Red (633nm)" package="5 mm [THT]"]
  R1 = Resistor [tolerance=±5% resistance=220 package=THT]
  R2 = Resistor [tolerance=±5% resistance=220 package=THT]
  S1 = Pushbutton [package="[THT]"]
  S2 = Pushbutton [package="[THT]"]
  S3 = Pushbutton [package="[THT]"]
  R3 = Resistor [tolerance=±5% resistance=220 package=THT]
  R4 = Resistor [tolerance=±5% resistance=4.7k package=THT]
  R5 = Resistor [tolerance=±5% resistance=4.7k package=THT]
  R6 = Resistor [tolerance=±5% resistance=4.7k package=THT]

nets:
  GND: Part1.GND, JP1_(X-end).1, JP2_(Y-end).1, JP3_(laser/servo).1, JP6_(step_pwr).2, JP7_(step_pwr).2, JP8_(power_in).2, R1.Pin_0, R2.Pin_0, R4.Pin_0, R5.Pin_0, R6.Pin_0
  N1: Part1.D3, JP5_(x-stepper).1
  N2: Part1.D4, JP5_(x-stepper).2
  N3: Part1.D5, JP5_(x-stepper).3
  N4: Part1.D6, JP5_(x-stepper).4
  N5: Part1.D7, JP4_(Y-stepper).1
  N6: Part1.D8, JP4_(Y-stepper).2
  N7: Part1.D9, JP4_(Y-stepper).3
  N8: Part1.D10, JP4_(Y-stepper).4
  N9: Part1.D11/MOSI, JP3_(laser/servo).3
  5V: Part1.5V, JP1_(X-end).2, JP2_(Y-end).2, JP3_(laser/servo).2, JP8_(power_in).3, R3.Pin_1
  N10: Part1.A5, JP1_(X-end).3, LED2.cathode
  N11: Part1.A4, JP2_(Y-end).3, LED1.cathode
  N12: Part1.A2, S1.Pin_1, S1.Pin_2, R4.Pin_1
  N13: Part1.A1, S2.Pin_1, S2.Pin_2, R5.Pin_1
  N14: Part1.A0, S3.Pin_1, S3.Pin_2, R6.Pin_1
  12V: JP6_(step_pwr).1, JP7_(step_pwr).1, JP8_(power_in).1
  N15: LED1.anode, R1.Pin_1
  N16: LED2.anode, R2.Pin_1
  N17: S1.Pin_3, S1.Pin_4, S2.Pin_3, S2.Pin_4, S3.Pin_3, S3.Pin_4, R3.Pin_0
